# Fritzing sketch Color sensor (saved by Fritzing 0.9.3b)
breadboards: 1

parts:
  MODULE1 = Color sensor TCS230
  Часть1 = Arduino Uno (Rev3)
  LED1 = RGB LED (com. cathode, rgb) [package="5 mm [THT]"]
  R1 = Resistor [tolerance=±5% resistance=220 package=THT]
  R2 = Resistor [tolerance=±5% resistance=220 package=THT]
  R3 = Resistor [tolerance=±5% resistance=220 package=THT]

nets:
  VCC: MODULE1.VCC, Часть1.5V
  N1: MODULE1.OUT, Часть1.D8
  N2: MODULE1.S2, Часть1.D6_PWM
  N3: MODULE1.S3, Часть1.D7
  N4: MODULE1.S0, Часть1.D4
  N5: MODULE1.S1, Часть1.D5_PWM
  GND: MODULE1.GND, Часть1.GND, LED1.common_cathode
  N6: Часть1.D9_PWM, R1.Pin_1
  N7: Часть1.D10_PWM/SS, R2.Pin_1
  N8: Часть1.D11_PWM/MOSI, R3.Pin_1
  N9: LED1.red_anode, R1.Pin_0
  N10: LED1.green_anode, R2.Pin_0
  N11: LED1.blue_anode, R3.Pin_0
