# Fritzing sketch Color sensor_scheme (saved by Fritzing 0.9.3b)
breadboards: 1

parts:
  TCS230 = Color sensor TCS230
  LED1 = RGB LED (com. cathode, rgb) [package="5 mm [THT]"]
  R1 = Resistor [tolerance=±5% resistance=220 package=THT]
  R2 = Resistor [tolerance=±5% resistance=220 package=THT]
  R3 = Resistor [tolerance=±5% resistance=220 package=THT]

nets:
  5V: TCS230.VCC
  Arduino 8: TCS230.OUT
  Arduino 6: TCS230.S2
  Arduino 7: TCS230.S3
  Arduino 4: TCS230.S0
  Arduino 5: TCS230.S1
  GND: TCS230.GND, LED1.common_cathode
  N1: LED1.red_anode, R1.Pin_1
  N2: LED1.green_anode, R2.Pin_1
  N3: LED1.blue_anode, R3.Pin_1
  Arduino 9: R1.Pin_0
  Arduino 10: R2.Pin_0
  Arduino 11: R3.Pin_0
